# Fritzing sketch final_circuit_strip (saved by Fritzing 0.9.3b)

parts:
  IC4 = MCP3008 8-channel 10-bit ADC [part_number=MCP3008]
  J13 = double row female pin header, 6 pins [form="♀ (female)"]
  J14 = double row female pin header, 6 pins [form="♀ (female)"]
  Part4 = Adafruit Perma-Proto HAT [part_number="Adafruit #2314 and #2310"]
  R5 = Resistor [tolerance=±5% resistance=4.7k package="0402 [SMD]"]
  R6 = Resistor [tolerance=±5% resistance=4.7k package="0402 [SMD]"]
  Part6 = Adafruit BME280

nets:
  N1: IC4.no_name_yet#1, Part4.N$1#160
  N2: IC4.no_name_yet#2, Part4.N$2
  N3: IC4.no_name_yet#3, Part4.N$3
  N4: IC4.no_name_yet#4, Part4.N$4
  N5: IC4.no_name_yet#5, Part4.N$5
  N6: IC4.no_name_yet#6, Part4.N$6
  N7: IC4.no_name_yet#7, Part4.N$8
  N8: IC4.no_name_yet#8, Part4.N$7
  N9: IC4.no_name_yet#9, Part4.N$55#344
  N10: IC4.no_name_yet#10, Part4.N$56#350
  N11: IC4.no_name_yet#11, Part4.N$57#355
  N12: IC4.no_name_yet#12, Part4.N$58#360
  N13: IC4.no_name_yet#13, Part4.N$60#370
  N14: IC4.no_name_yet#14, Part4.N$59#365
  N15: IC4.no_name_yet#15, Part4.N$61#375
  N16: IC4.no_name_yet#16, Part4.N$62#380
  N17: J13.pin1, Part4.N$10
  N18: J13.pin2, Part4.N$11#207
  N19: J13.pin3, Part4.N$12#212
  N20: J13.pin4, Part4.N$13#217
  N21: J13.pin5, Part4.N$14#222
  N22: J13.pin6, Part4.N$15#227
  N23: J14.pin1, Part4.N$45
  N24: J14.pin2, Part4.N$44#288
  N25: J14.pin3, Part4.N$43#283
  N26: J14.pin4, Part4.N$42#278
  N27: J14.pin5, Part4.N$41#273
  N28: J14.pin6, Part4.N$39
  N29: Part4.SDA, Part6.SDO/ADR
  N30: Part4.SCL, Part6.SCK/SCL
  N31: Part4.GPIO4, Part4.N$15#230
  N32: Part4.SPI_MOSI, Part4.N$57#351
  N33: Part4.SPI_MISO, Part4.N$58#356
  N34: Part4.SPI_SCLK, Part4.N$60#366
  N35: Part4.SPI_CE0, Part4.N$56#346
  N36: Part4.GPIO5, Part4.N$43#281
  N37: Part4.GPIO6, Part4.N$13#220
  3.3V: Part4.3.3V, Part4.N$11#208, Part4.N$44#286, Part4.N$61#371, Part4.N$62#376, Part6.3.3V
  GND: Part4.GND, Part4.N$12#211, Part4.N$14#221, Part4.N$42#276, Part4.N$55#341, Part4.N$59#361, R5.Pin_1, Part6.GND
  N38: Part4.N$1#159, Part4.N$47#305
  N39: Part4.N$11#209, R6.Pin_1
  N40: Part4.N$15#229, R6.Pin_0
  N41: Part4.N$41#274, Part4.N$47#304, R5.Pin_0

custom parts:
  Adafruit Perma-Proto HAT: To kick off the Adafruit HAT party, we have this Perma-Proto inspired plug in daughter board. It has a grid of 0.1" prototyping soldering holes for attaching chips, resistors, LED, potentiometers and more. The holes are connected underneath with traces to mimic the solderless breadboards you're familiar. There's also long power strips for +3V, +5V and Ground connections to the Pi. Near the top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
  Adafruit BME280: Bosch has stepped up their game with their new BME280 sensor, an environmental sensor with temperature, barometric pressure and humidity! This sensor is great for all sorts of weather/environmental sensing and can even be used in both I2C and SPI! This precision sensor from Bosch is the best low-cost sensing solution for measuring humidity with ±3% accuracy, barometric pressure with ±1 hPa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
